# Fritzing sketch rp5-proj-schematic (saved by Fritzing 1.0.0rc)
breadboards: 1

parts:
  Mod1 = Raspberry Pi 4B
  LED1 = LED - 5mm [color="Red (633nm)" current=0.030A package="5 mm [THT]"]
  LED2 = LED - 5mm [color="Red (633nm)" current=0.030A package="5 mm [THT]"]
  R1 = Resistor [tolerance=±5% resistance=100 package="0805 [SMD]"]
  R2 = Resistor [tolerance=±5% resistance=100 package="0805 [SMD]"]
  S1 = Pushbutton [package="[THT]"]

nets:
  N1: Mod1.GND, R1.Pin_1, R2.Pin_1, S1.Pin_1, S1.Pin_2
  N2: Mod1.GPIO14, S1.Pin_3, S1.Pin_4
  N3: Mod1.GPIO17, LED2.anode
  N4: Mod1.GPIO11, LED1.anode
  N5: LED1.cathode, R2.Pin_0
  N6: LED2.cathode, R1.Pin_0
